// Logisim project FFd_ena_rst.circ as structural Verilog: 1 circuit, main circuit ff_d_ena_rst
module ff_d_ena_rst (
  input  D,
  input  ENA,
  input  RST,
  input  CLK,
  output SALIDA
);

  wire multiplexer_1_out, multiplexer_2_out;

  Multiplexer multiplexer_1 (.in0(SALIDA), .in1(D), .out(multiplexer_1_out), .sel(ENA));
  D_Flip_Flop d_ff_1 (.D(multiplexer_2_out), .clk(CLK), .Q(SALIDA));  // open: Qn, preset, reset
  Multiplexer multiplexer_2 (.in0(multiplexer_1_out), .in1(1'b0), .out(multiplexer_2_out), .sel(RST));
endmodule
